// Logisim project One_Instruction_Processing_Unit.circ as structural Verilog: 1 circuit, main circuit main
module main (
  input  in_1
);

  wire clock_1_out, decoder_1_out0, decoder_1_out2, decoder_1_out3, nor_1_out;
  wire [1:0] counter_1_q;
  wire [7:0] adder_1_out, multiplexer_1_out, multiplexer_2_out, nand_1_out, ram_1_data, register_1_q,
       register_2_q, rom_1_data, rom_1_data_2;
  wire [16:16] rom_1_data_3;

  Clock clock_1 (.out(clock_1_out));
  Multiplexer #(.width(8)) multiplexer_1 (
    .in0(rom_1_data), .in1(rom_1_data_2), .out(multiplexer_1_out), .sel(nor_1_out), .en(1'b1));
  Decoder #(.select(2)) decoder_1 (
    .out0(decoder_1_out0), .out2(decoder_1_out2), .out3(decoder_1_out3), .sel(counter_1_q), .en(1'b1));  // open: out1
  Counter #(.width(2), .max('h3)) counter_1 (
    .count(1'b1), .Q(counter_1_q), .clk(clock_1_out), .clr(in_1));  // open: load, D, carry
  Register register_1 (.D(adder_1_out), .Q(register_1_q), .clk(decoder_1_out3), .clr(in_1));  // open: en
  Adder adder_1 (.a(register_1_q), .b(8'h1), .out(adder_1_out));  // open: cin, cout
  not nor_1 (nor_1_out, decoder_1_out0);  // NOR_Gate
  RAM #(.bus("separate")) ram_1 (
    .addr(multiplexer_1_out), .din(nand_1_out), .data(ram_1_data), .str(decoder_1_out2), .clk(clock_1_out),
    .ld(1'b1), .clr(in_1));  // open: sel
  ROM #(.dataWidth(17)) rom_1 (.addr(register_1_q), .data({rom_1_data_3[16], rom_1_data_2, rom_1_data}));  // open: sel
  Register register_2 (.D(ram_1_data), .en(decoder_1_out0), .Q(register_2_q), .clk(clock_1_out));  // open: clr
  Multiplexer #(.width(8)) multiplexer_2 (
    .in0(rom_1_data_2), .in1(ram_1_data), .out(multiplexer_2_out), .sel(rom_1_data_3[16]), .en(1'b1));
  assign nand_1_out = ~(register_2_q & multiplexer_2_out);  // NAND_Gate nand_1, 8 bits wide
endmodule
